# Fritzing sketch Chilling HelmetV2 (saved by Fritzing 0.9.3b)
breadboards: 1

parts:
  DHT1 = DHT22 Humidity and Temperature Sensor
  DHT4 = DHT22 Humidity and Temperature Sensor
  DHT5 = DHT22 Humidity and Temperature Sensor
  DHT6 = DHT22 Humidity and Temperature Sensor
  DHT7 = DHT22 Humidity and Temperature Sensor
  DHT8 = DHT22 Humidity and Temperature Sensor
  DHT9 = DHT22 Humidity and Temperature Sensor
  DHT10 = DHT22 Humidity and Temperature Sensor
  DHT11 = DHT22 Humidity and Temperature Sensor
  Part1 = Arduino Uno (Rev3)
  M1 = DC Motor
  Relay = IC, DIP package, 6 pins [chip_label=IC]
  Power_plug1 = Power plug

nets:
  VDD: DHT1.VDD, DHT4.VDD, DHT5.VDD, DHT6.VDD, DHT7.VDD, DHT8.VDD, DHT9.VDD, DHT10.VDD, DHT11.VDD, Part1.5V
  N1: DHT1.DATA, Part1.D4
  GND: DHT1.GND, DHT4.GND, DHT5.GND, DHT6.GND, DHT7.GND, DHT8.GND, DHT9.GND, DHT10.GND, DHT11.GND, Part1.GND, M1.pin_2
  N2: DHT4.DATA, Part1.D5_PWM
  N3: DHT5.DATA, Part1.D3_PWM
  N4: DHT6.DATA, Part1.D6_PWM
  N5: DHT7.DATA, Part1.D7
  N6: DHT8.DATA, Part1.D8
  N7: DHT9.DATA, Part1.D9_PWM
  N8: DHT10.DATA, Part1.D2
  N9: DHT11.DATA, Part1.D10_PWM/SS
  N10: Part1.D12/MISO, Relay.pin2
  N11: M1.pin_1, Relay.pin6
  N12: Relay.pin3, Power_plug1.GND
  N13: Relay.pin5, Power_plug1.VCC

notes:
  Rechargeable 12 V Power Supply
  Relay
  DC Pump(Yellow=ground, green= live)
  DHT22
  I wasn't sure how to use the arduino to turn on/off the pump if we are to use a 12V power supply. Instead I'm connecting the step-up to an output pin of the arduino and then connecting the pump to the step up via a relay.
